# Fritzing sketch Esquema del dispositiu (saved by Fritzing 0.9.4)

parts:
  U1 = RFID RC522 SIP - 8 pins [chip_label="RFID RC522" package="SIP (Single Inline) [THT]"]
  LCD1 = LCD screen
  LCM1602_IIC1 = LCM1602 IIC [part_number="LCM1602 IIC" chip_label="LCM1602 IIC" package="DIP (Dual Inline) [THT]"]
  WeMos_D1_R1 = WeMos D1 R2

nets:
  N1: U1.NSS, WeMos_D1_R1.D10
  N2: U1.SCK, WeMos_D1_R1.D13
  N3: U1.MOSI, WeMos_D1_R1.D11
  N4: U1.MISO, WeMos_D1_R1.D12
  N5: U1.GND, WeMos_D1_R1.GND#15
  N6: U1.RST, WeMos_D1_R1.D2
  VCC: U1.VCC, WeMos_D1_R1.3.3V
  VSS: LCD1.VSS, LCM1602_IIC1.VSS
  VDD: LCD1.VDD, LCM1602_IIC1.VDD
  N7: LCD1.V0, LCM1602_IIC1.V0
  N8: LCD1.RS, LCM1602_IIC1.RS
  N9: LCD1.R/W, LCM1602_IIC1.RW
  N10: LCD1.E, LCM1602_IIC1.E
  N11: LCD1.DB0, LCM1602_IIC1.D0
  N12: LCD1.DB1, LCM1602_IIC1.D1
  N13: LCD1.DB2, LCM1602_IIC1.D2
  N14: LCD1.DB3, LCM1602_IIC1.D3
  N15: LCD1.DB4, LCM1602_IIC1.D4
  N16: LCD1.DB5, LCM1602_IIC1.D5
  N17: LCD1.DB6, LCM1602_IIC1.D6
  N18: LCD1.DB7, LCM1602_IIC1.D7
  N19: LCD1.LED+, LCM1602_IIC1.A
  N20: LCD1.LED-, LCM1602_IIC1.K
  N21: LCM1602_IIC1.GND, WeMos_D1_R1.GND#21
  VCC_2: LCM1602_IIC1.VCC, WeMos_D1_R1.5V
  N22: LCM1602_IIC1.SDA, WeMos_D1_R1.D14
  N23: LCM1602_IIC1.SCL, WeMos_D1_R1.D15

custom parts:
  RFID RC522 SIP - 8 pins: A SIP stand-in part for RFID RC522 . With 8 pins on a 300 mil single inline package (SIP) footprint.
  LCM1602 IIC: I2C-Module to use a 1602 or 2004 LCD on with the wire.h libory Serial LCD Modul
  WeMos D1 R2: The D1 R2 is a mini wifi board based on the ESP-8266EX.
