# Fritzing sketch lector_rfid (saved by Fritzing 0.9.3b)

parts:
  Componente4 = Arduino Uno (Rev3)
  U1 = RFID RC522 SIP - 8 pins [chip_label="RFID RC522" package="SIP (Single Inline) [THT]"]
  Pro_Micro1 = Pro Micro

nets:
  N1: Componente4.D9_PWM, U1.RST
  N2: Componente4.D10_PWM/SS, U1.NSS
  N3: Componente4.D11_PWM/MOSI, U1.MOSI
  N4: Componente4.D12/MISO, U1.MISO
  N5: Componente4.D13/SCK, U1.SCK
  N6: Componente4.A4/SDA, Pro_Micro1.D2
  N7: Componente4.A5/SCL, Pro_Micro1.D3
  3V3: Componente4.3V3, U1.VCC
  GND: Componente4.GND, U1.GND, Pro_Micro1.GND
  VIN: Componente4.VIN, Pro_Micro1.VCC

custom parts:
  RFID RC522 SIP - 8 pins: A SIP stand-in part for RFID RC522 . With 8 pins on a 300 mil single inline package (SIP) footprint.
  Pro Micro: The SparkFun Pro Micro is a complete USB-based microcontoller development system, in a very small footprint, capable of implementing many types of projects. All programming can be done via the USB port.
